// Digital circuit 8bit_alu.dig as structural Verilog
module _8bit_alu (
  input  [7:0] A,
  input  [7:0] B,
  input  [2:0] OP,
  input  CLK,
  input  WFLAGEN,
  input  CLR,
  output [7:0] FLAGS,
  output [7:0] RESULT
);

  wire or_1_out;
  wire [4:0] nand_1_out;
  wire [7:0] _8bit_add_sub_1_result, _8bit_or_nor_xor_and_1_out;

  _8bit_register_async_clear _8bit_register_async_clear_1 (
    .CLK(CLK), .WEN(WFLAGEN), .WRITE({3'b000, nand_1_out[4], RESULT[7], nand_1_out[2:0]}), .CLR(CLR),
    .READ(FLAGS));
  _8bit_add_sub _8bit_add_sub_1 (
    .A(A), .B(B), .ADD_SUB(OP[1]), .ADC_SBC(OP[0]), .CIN(FLAGS[0]), .RESULT(_8bit_add_sub_1_result),
    .COUT(nand_1_out[0]), .OVF(nand_1_out[1]));
  _8bit_or_nor_xor_and _8bit_or_nor_xor_and_1 (
    .SEL(OP[1:0]), .A(A), .B(B), .OUT(_8bit_or_nor_xor_and_1_out), .EQUAL(nand_1_out[2]));
  _2x8bit_mux _2x8bit_mux_1 (.SEL(OP[2]), .B(_8bit_or_nor_xor_and_1_out), .A(_8bit_add_sub_1_result), .OUT(RESULT));
  or or_1 (or_1_out, RESULT[0], RESULT[1], RESULT[2], RESULT[3], RESULT[4], RESULT[5], RESULT[6], RESULT[7]);
  nand nand_1 (nand_1_out[4], or_1_out, or_1_out);

  // Notes on the sheet:
  //   Schottky Diode OR
endmodule
