// Digital circuit cpu.dig as structural Verilog
module cpu (
  input  CLK,
  input  RESET,
  input  HALT,
  input  CONTINUE,
  output IOEN,
  output IOREN,
  output IOWEN,
  output [7:0] IODATA,
  output [14:0] IOADDR
);

  wire condition_checker_1_skip, nand_1_out, nand_2_out, nand_3_out, nand_4_out, nand_5_out, nand_6_out,
       nand_7_out, nand_8_out, nand_9_out, nand_10_out, nand_11_out, nand_12_out, nand_13_out, nand_14_out,
       nand_15_out, nand_16_out, nand_17_out, nand_18_out, nand_19_out, nand_20_out, nand_21_out,
       nand_22_out, nand_23_out, nand_24_out, nand_25_out, nand_26_out, nand_27_out, oprom_1_bssel,
       oprom_1_fwen, oprom_1_halt, oprom_1_massel, oprom_1_rwen;
  wire [1:0] oprom_1_pcssel, oprom_1_rssel, program_memory_1_rd, program_memory_1_ro1, program_memory_1_ro2;
  wire [2:0] program_memory_1_aluop, program_memory_1_cond;
  wire [3:0] program_memory_1_opcode;
  wire [4:0] _8bit_alu_1_flags;
  wire [7:0] _2x8bit_mux_1_out, _2x16bit_mux_1_p2_2, _4x8bit_mux_1_out, _8bit_alu_1_result,
       program_memory_1_imm8;
  wire [7:5] _8bit_alu_1_flags_2;
  wire [15:0] _2x16bit_mux_1_p2, _4x16bit_mux_1_out, _16bit_incrementer_1_out, program_counter_1_r,
       program_memory_1_imm16;

  LED u_HALT (.in(nand_7_out));
  nand nand_1 (nand_1_out, HALT, HALT);
  nand nand_2 (nand_2_out, RESET, RESET);
  nand nand_3 (nand_3_out, nand_10_out, nand_10_out);
  nand nand_4 (nand_4_out, nand_11_out, nand_11_out);
  nand nand_5 (nand_5_out, nand_1_out, nand_2_out);
  nand nand_6 (nand_6_out, nand_4_out, CONTINUE);
  nand nand_7 (nand_7_out, nand_4_out, nand_8_out);
  nand nand_8 (nand_8_out, nand_7_out, nand_6_out);
  nand nand_9 (nand_9_out, nand_5_out, nand_5_out);
  nand nand_10 (nand_10_out, nand_12_out, nand_12_out);
  nand nand_11 (nand_11_out, nand_9_out, nand_3_out);
  nand nand_12 (nand_12_out, nand_15_out, oprom_1_halt);
  nand nand_13 (nand_13_out, CLK, nand_8_out);
  nand nand_14 (nand_14_out, nand_13_out, nand_13_out);
  nand nand_15 (nand_15_out, CLK, CLK);
  nand nand_16 (nand_16_out, nand_14_out, nand_14_out);
  nand nand_17 (nand_17_out, RESET, RESET);
  program_memory program_memory_1 (
    .ADR(program_counter_1_r), .OPCODE(program_memory_1_opcode), .COND(program_memory_1_cond),
    .ALUOP(program_memory_1_aluop), .RD(program_memory_1_rd), .RO1(program_memory_1_ro1),
    .RO2(program_memory_1_ro2), .IMM8(program_memory_1_imm8), .IMM16(program_memory_1_imm16));
  program_counter program_counter_1 (
    .CLK(nand_14_out), .W(_4x16bit_mux_1_out), .CLR(nand_17_out), .R(program_counter_1_r));
  _4x16bit_mux _4x16bit_mux_1 (
    .SEL(oprom_1_pcssel), .IN0({16{1'b0}}), .IN1(_16bit_incrementer_1_out), .IN2(_2x16bit_mux_1_p2),
    .IN3(program_memory_1_imm16), .OUT(_4x16bit_mux_1_out));
  condition_checker condition_checker_1 (
    .FLAGS(_8bit_alu_1_flags), .COND(program_memory_1_cond), .SKIP(condition_checker_1_skip));
  oprom oprom_1 (
    .OPCODE(program_memory_1_opcode), .SKIP(condition_checker_1_skip), .RWEN(oprom_1_rwen),
    .FWEN(oprom_1_fwen), .MREN(IOREN), .MWEN(IOWEN), .BSSEL(oprom_1_bssel), .MASSEL(oprom_1_massel),
    .RSSEL(oprom_1_rssel), .PCSSEL(oprom_1_pcssel), .HALT(oprom_1_halt));
  _16bit_incrementer _16bit_incrementer_1 (.IN(program_counter_1_r), .OUT(_16bit_incrementer_1_out));
  _4x8bit_mux _4x8bit_mux_1 (
    .SEL(oprom_1_rssel), .IN0(program_memory_1_imm8), .IN1(IODATA), .IN2(_8bit_alu_1_result),
    .IN3(_2x16bit_mux_1_p2[7:0]), .OUT(_4x8bit_mux_1_out));
  // _2x16bit_mux _2x16bit_mux_1: pin names not known; wires that end beside it: oprom_1_massel, {_2x16bit_mux_1_p2_2, _2x16bit_mux_1_p2[7:0]}, program_memory_1_imm16, {IOEN, IOADDR}
  _4x8bit_register_file_async_clear _4x8bit_register_file_async_clear_1 (
    .CLK(nand_16_out), .WEN(oprom_1_rwen), .WRITE(_4x8bit_mux_1_out), .R1SEL(program_memory_1_ro1),
    .WSEL(program_memory_1_rd), .R2SEL(program_memory_1_ro2), .CLR(nand_17_out),
    .READ1(_2x16bit_mux_1_p2[7:0]), .READ2(_2x16bit_mux_1_p2[15:8]), .READP(_2x16bit_mux_1_p2_2));
  nand nand_18 (nand_18_out, IOEN, IOEN);
  _2x8bit_mux _2x8bit_mux_1 (
    .SEL(oprom_1_bssel), .B(_2x16bit_mux_1_p2[15:8]), .A(program_memory_1_imm8), .OUT(_2x8bit_mux_1_out));
  nand nand_19 (nand_19_out, IOWEN, nand_18_out);
  nand nand_20 (nand_20_out, IOREN, nand_18_out);
  _8bit_alu _8bit_alu_1 (
    .A(_2x16bit_mux_1_p2[7:0]), .B(_2x8bit_mux_1_out), .OP(program_memory_1_aluop), .CLK(nand_16_out),
    .WFLAGEN(oprom_1_fwen), .FLAGS({_8bit_alu_1_flags_2, _8bit_alu_1_flags}), .RESULT(_8bit_alu_1_result));
  nand nand_21 (nand_21_out, nand_19_out, nand_19_out);
  nand nand_22 (nand_22_out, nand_20_out, nand_20_out);
  nand nand_23 (nand_23_out, nand_21_out, nand_16_out);
  nand nand_24 (nand_24_out, IOREN, IOREN);
  nand nand_25 (nand_25_out, nand_23_out, nand_23_out);
  nand nand_26 (nand_26_out, IOWEN, nand_24_out);
  nand nand_27 (nand_27_out, nand_26_out, nand_26_out);
  RAMSinglePortSel #(.AddrBits(15), .Bits(8)) ramsingleportsel_1 (
    .A(IOADDR), .CS(1'b1), .WE(nand_25_out), .OE(nand_22_out), .D(IODATA));
  assign IODATA = nand_27_out ? _2x16bit_mux_1_p2[15:8] : 8'bz;  // Driver driver_1

  // Notes on the sheet:
  //   CLK: Hz: 10
endmodule
