// Digital circuit oprom.dig as structural Verilog
module oprom (
  input  [3:0] OPCODE,
  input  SKIP,
  output RWEN,
  output FWEN,
  output MWEN,
  output BSSEL,
  output MASSEL,
  output [1:0] RSSEL,
  output [1:0] PCSSEL
);

  wire nand_1_out, nand_2_out, nand_3_out, nand_4_out, nand_5_out;
  wire [3:0] nand_6_out;

  nand nand_1 (nand_1_out, SKIP, SKIP);
  nand nand_2 (nand_2_out, nand_1_out, OPCODE[0]);
  nand nand_3 (nand_3_out, nand_1_out, OPCODE[1]);
  nand nand_4 (nand_4_out, nand_1_out, OPCODE[2]);
  nand nand_5 (nand_5_out, nand_1_out, OPCODE[3]);
  nand nand_6 (nand_6_out[0], nand_2_out, nand_2_out);
  nand nand_7 (nand_6_out[1], nand_3_out, nand_3_out);
  nand nand_8 (nand_6_out[2], nand_4_out, nand_4_out);
  nand nand_9 (nand_6_out[3], nand_5_out, nand_5_out);
  _16x9bit_mux _16x9bit_mux_1 (
    .SEL(nand_6_out), .IN0(9'h80), .IN1({9{1'b0}}), .IN2({9{1'b0}}), .IN3({9{1'b0}}), .IN4({9{1'b0}}),
    .IN5({9{1'b0}}), .IN6(9'h81), .IN7({9{1'b0}}), .IN8({9{1'b0}}), .IN9(9'hcb), .IN10({9{1'b0}}),
    .IN11({9{1'b0}}), .IN12({9{1'b0}}), .IN13({9{1'b0}}), .IN14({9{1'b0}}), .IN15({9{1'b0}}),
    .OUT({PCSSEL, RSSEL, MASSEL, BSSEL, MWEN, FWEN, RWEN}));
endmodule
