// Digital circuit program_memory.dig as structural Verilog
module program_memory (
  input  [15:0] ADR,
  output [3:0] OPCODE,
  output [2:0] COND,
  output [2:0] ALUOP,
  output [1:0] RD,
  output [1:0] RO1,
  output [1:0] RO2,
  output [7:0] IMM8,
  output [15:0] IMM16
);

  ROM #(.AddrBits(16), .Bits(32)) rom_1 (
    .A(ADR), .sel(1'b1), .D({OPCODE, COND, ALUOP, RD, RO1, RO2, IMM16[15:8], IMM8}));

  assign IMM16[7:0] = IMM8;

  // Notes on the sheet:
  //   contents of rom_1 (hex, n*v repeats v):
  //   0,60805500,60405500,90110000
endmodule
